// Logisim project 1.circ as structural Verilog: 2 circuits, main circuit main
module main (
  input  A,
  input  B,
  input  Bin,
  output D,
  output Bout
);

  wire and_1_out, and_2_out, and_3_out, and_4_out, and_5_out, and_6_out, and_7_out, and_8_out, not_1_out,
       not_2_out, not_3_out;

  not not_1 (not_1_out, A);
  not not_2 (not_2_out, B);
  not not_3 (not_3_out, Bin);
  and and_1 (and_1_out, not_1_out, not_2_out, Bin);
  and and_2 (and_2_out, not_1_out, B, not_3_out);
  and and_3 (and_3_out, A, not_2_out, not_3_out);
  and and_4 (and_4_out, A, B, Bin);
  and and_5 (and_5_out, not_1_out, not_2_out, Bin);
  and and_6 (and_6_out, not_1_out, B, not_3_out);
  and and_7 (and_7_out, not_1_out, B, Bin);
  and and_8 (and_8_out, A, B, Bin);
  or or_1 (D, and_1_out, and_2_out, and_3_out, and_4_out);
  or or_2 (Bout, and_5_out, and_6_out, and_7_out, and_8_out);
endmodule

module BIT8 (
  input  in_1,
  input  in_2,
  input  in_3,
  input  in_4,
  input  in_5,
  output out_6,
  output out_7,
  output out_8,
  output out_9
);

  main main_1 (.A(in_2), .B(in_3), .Bin(in_1), .D(out_6), .Bout(out_7));
  main main_2 (.A(in_4), .B(in_5), .D(out_8), .Bout(out_9));  // open: Bin
endmodule
