// Logisim project 1_BIT8_fixed.circ as structural Verilog: 2 circuits, main circuit BIT8
module main (
  input  A,
  input  B,
  input  Bin,
  output D,
  output Bout
);

  wire and_1_out, and_2_out, and_3_out, and_4_out, and_5_out, and_6_out, and_7_out, and_8_out, not_1_out,
       not_2_out, not_3_out;

  not not_1 (not_1_out, A);
  not not_2 (not_2_out, B);
  not not_3 (not_3_out, Bin);
  and and_1 (and_1_out, not_1_out, not_2_out, Bin);
  and and_2 (and_2_out, not_1_out, B, not_3_out);
  and and_3 (and_3_out, A, not_2_out, not_3_out);
  and and_4 (and_4_out, A, B, Bin);
  and and_5 (and_5_out, not_1_out, not_2_out, Bin);
  and and_6 (and_6_out, not_1_out, B, not_3_out);
  and and_7 (and_7_out, not_1_out, B, Bin);
  and and_8 (and_8_out, A, B, Bin);
  or or_1 (D, and_1_out, and_2_out, and_3_out, and_4_out);
  or or_2 (Bout, and_5_out, and_6_out, and_7_out, and_8_out);
endmodule

module BIT8 (
  input  A0,
  input  B0,
  input  Bin,
  input  A1,
  input  B1,
  input  A2,
  input  B2,
  input  A3,
  input  B3,
  input  A4,
  input  B4,
  input  A5,
  input  B5,
  input  A6,
  input  B6,
  input  A7,
  input  B7,
  output D0,
  output D1,
  output D2,
  output D3,
  output D4,
  output D5,
  output D6,
  output D7,
  output Bout
);

  wire main_6_bout, main_8_bout;

  main main_1 (.A(A0), .B(B0), .Bin(Bin), .D(D0), .Bout(D0));
  main main_2 (.A(A2), .B(B2), .Bin(main_8_bout), .D(D2), .Bout(D2));
  main main_3 (.A(A3), .B(B3), .Bin(D2), .D(D3), .Bout(D3));
  main main_4 (.A(A4), .B(B4), .Bin(D3), .D(D4), .Bout(D4));
  main main_5 (.A(A5), .B(B5), .Bin(A6), .D(D5), .Bout(D5));
  main main_6 (.A(A6), .B(B6), .Bin(D5), .D(D6), .Bout(main_6_bout));
  main main_7 (.A(A7), .B(B7), .Bin(main_6_bout), .D(D7), .Bout(Bout));
  main main_8 (.A(A1), .B(B1), .Bin(D0), .D(D1), .Bout(main_8_bout));
endmodule
